// Logisim project Somador32Bits.circ as structural Verilog
module SomadorCompleto (
  input  Cin,
  input  A,
  input  B,
  output S,
  output Cout
);

  wire and_1_out, and_2_out, xor_1_out;

  xor xor_1 (xor_1_out, A, B);
  and and_1 (and_1_out, A, B);
  or or_1 (Cout, and_1_out, and_2_out);
  xor xor_2 (S, xor_1_out, Cin);
  and and_2 (and_2_out, xor_1_out, Cin);

  // Notes on the sheet:
  //   Somador Completo
  //   Fernando Campos Silva Dal Maria - 765053
endmodule

module Somador4Bits (
  input  Cin,
  input  [3:0] A,
  input  [3:0] B,
  output [3:0] S,
  output Cout
);

  wire somadorcompleto_1_cout, somadorcompleto_2_cout, somadorcompleto_3_cout;

  SomadorCompleto somadorcompleto_1 (.Cin(Cin), .A(A[0]), .B(B[0]), .S(S[0]), .Cout(somadorcompleto_1_cout));
  SomadorCompleto somadorcompleto_2 (
    .Cin(somadorcompleto_1_cout), .A(A[1]), .B(B[1]), .S(S[1]), .Cout(somadorcompleto_2_cout));
  SomadorCompleto somadorcompleto_3 (
    .Cin(somadorcompleto_2_cout), .A(A[2]), .B(B[2]), .S(S[2]), .Cout(somadorcompleto_3_cout));
  SomadorCompleto somadorcompleto_4 (.Cin(somadorcompleto_3_cout), .A(A[3]), .B(B[3]), .S(S[3]), .Cout(Cout));

  // Notes on the sheet:
  //   Somador Completo 4 bits
  //   Fernando Campos Silva Dal Maria - 765053
endmodule

module Decodificador (
  input  E3,
  input  E2,
  input  E1,
  input  E0,
  output a,
  output b,
  output c,
  output d,
  output e,
  output f,
  output g
);

  wire and_1_out, and_2_out, and_3_out, and_4_out, and_5_out, and_6_out, and_7_out, and_8_out, and_9_out,
       and_10_out, and_11_out, and_12_out, and_13_out, and_14_out, and_15_out, and_16_out, and_17_out,
       and_18_out, and_19_out, and_20_out, and_21_out, and_22_out, and_23_out, and_24_out, and_25_out,
       and_26_out, and_27_out, and_28_out, and_29_out, and_30_out, and_31_out, and_32_out, and_33_out,
       and_34_out, and_35_out, and_36_out, and_37_out, and_38_out, and_39_out, and_40_out, not_1_out,
       not_2_out, not_3_out, not_4_out;

  not not_1 (not_1_out, E3);
  not not_2 (not_2_out, E2);
  not not_3 (not_3_out, E1);
  not not_4 (not_4_out, E0);
  and and_1 (and_1_out, not_2_out, not_4_out);
  and and_2 (and_2_out, not_1_out, E1);
  and and_3 (and_3_out, not_1_out, E2, E0);
  and and_4 (and_4_out, E3, not_2_out, not_3_out);
  and and_5 (and_5_out, E3, not_4_out);
  and and_6 (and_6_out, E2, E1);
  and and_7 (and_7_out, not_1_out, not_3_out, not_4_out);
  and and_8 (and_8_out, not_1_out, E1, E0);
  and and_9 (and_9_out, not_2_out, not_4_out);
  and and_10 (and_10_out, E3, not_3_out, E0);
  and and_11 (and_11_out, not_1_out, not_2_out);
  and and_12 (and_12_out, not_1_out, E2);
  and and_13 (and_13_out, E3, not_2_out);
  and and_14 (and_14_out, not_3_out, E0);
  and and_15 (and_15_out, not_1_out, not_3_out);
  and and_16 (and_16_out, not_1_out, E0);
  and and_17 (and_17_out, E2, not_3_out, E0);
  and and_18 (and_18_out, not_1_out, not_2_out, not_4_out);
  and and_19 (and_19_out, not_1_out, not_2_out, E1);
  and and_20 (and_20_out, not_1_out, E1, not_4_out);
  and and_21 (and_21_out, not_2_out, not_3_out, not_4_out);
  and and_22 (and_22_out, E3, not_3_out);
  and and_23 (and_23_out, not_2_out, E1, E0);
  and and_24 (and_24_out, E2, E1, not_4_out);
  and and_25 (and_25_out, not_2_out, not_4_out);
  and and_26 (and_26_out, E1, not_4_out);
  and and_27 (and_27_out, E3, E1);
  and and_28 (and_28_out, E3, E2);
  and and_29 (and_29_out, not_3_out, not_4_out);
  and and_30 (and_30_out, not_1_out, E2, not_3_out);
  and and_31 (and_31_out, E2, not_4_out);
  and and_32 (and_32_out, E3, not_2_out);
  and and_33 (and_33_out, E3, E1);
  and and_34 (and_34_out, not_2_out, E1);
  and and_35 (and_35_out, E3, not_2_out);
  and and_36 (and_36_out, not_1_out, E2, not_3_out);
  and and_37 (and_37_out, not_1_out, E2, not_4_out);
  and and_38 (and_38_out, E2, not_3_out, E0);
  and and_39 (and_39_out, E1, not_4_out);
  and and_40 (and_40_out, E3, E0);
  or or_1 (a, and_1_out, and_2_out, and_3_out, and_4_out, and_5_out, and_6_out);
  or or_2 (b, and_7_out, and_8_out, and_9_out, and_10_out, and_11_out);
  or or_3 (c, and_12_out, and_13_out, and_14_out, and_15_out, and_16_out);
  or or_4 (d, and_17_out, and_18_out, and_19_out, and_20_out, and_21_out, and_22_out, and_23_out, and_24_out);
  or or_5 (e, and_25_out, and_26_out, and_27_out, and_28_out);
  or or_6 (f, and_29_out, and_30_out, and_31_out, and_32_out, and_33_out);
  or or_7 (g, and_34_out, and_35_out, and_36_out, and_37_out, and_38_out, and_39_out, and_40_out);
endmodule

module Somador16Bits (
  input  Cin,
  input  [15:0] A,
  input  [15:0] B,
  output [15:0] S,
  output Cout
);

  wire somador4bits_1_cout, somador4bits_2_cout, somador4bits_3_cout;

  Somador4Bits somador4bits_1 (.Cin(Cin), .A(A[3:0]), .B(B[3:0]), .S(S[3:0]), .Cout(somador4bits_1_cout));
  Somador4Bits somador4bits_2 (
    .Cin(somador4bits_1_cout), .A(A[7:4]), .B(B[7:4]), .S(S[7:4]), .Cout(somador4bits_2_cout));
  Somador4Bits somador4bits_3 (
    .Cin(somador4bits_2_cout), .A(A[11:8]), .B(B[11:8]), .S(S[11:8]), .Cout(somador4bits_3_cout));
  Somador4Bits somador4bits_4 (.Cin(somador4bits_3_cout), .A(A[15:12]), .B(B[15:12]), .S(S[15:12]), .Cout(Cout));

  // Notes on the sheet:
  //   Somador Completo 16 bits
  //   Fernando Campos Silva Dal Maria - 765053
endmodule

module Somador32Bits (
  input  Cin,
  input  [31:0] A,
  input  [31:0] B,
  output [31:0] S,
  output Cout
);

  wire somador16bits_1_cout;

  Somador16Bits somador16bits_1 (.Cin(Cin), .A(A[15:0]), .B(B[15:0]), .S(S[15:0]), .Cout(somador16bits_1_cout));
  Somador16Bits somador16bits_2 (.Cin(somador16bits_1_cout), .A(A[31:16]), .B(B[31:16]), .S(S[31:16]), .Cout(Cout));

  // Notes on the sheet:
  //   Somador Completo 32 Bits
  //   Fernando Campos Silva Dal Maria - 765053
endmodule

module Calculadora_Soma (
  input  A0,
  input  A1,
  input  A2,
  input  A3,
  input  B0,
  input  B1,
  input  B2,
  input  B3,
  output Cout,
  output Overflow
);

  wire decodificador_1_a, decodificador_1_b, decodificador_1_c, decodificador_1_d, decodificador_1_e,
       decodificador_1_f, decodificador_1_g, decodificador_2_a, decodificador_2_b, decodificador_2_c,
       decodificador_2_d, decodificador_2_e, decodificador_2_f, decodificador_2_g, decodificador_3_a,
       decodificador_3_b, decodificador_3_c, decodificador_3_d, decodificador_3_e, decodificador_3_f,
       decodificador_3_g;
  wire [3:0] somador4bits_1_s;

  Decodificador decodificador_1 (
    .E3(A3), .E2(A2), .E1(A1), .E0(A0), .a(decodificador_1_a), .b(decodificador_1_b), .c(decodificador_1_c),
    .d(decodificador_1_d), .e(decodificador_1_e), .f(decodificador_1_f), .g(decodificador_1_g));
  Decodificador decodificador_2 (
    .E3(B3), .E2(B2), .E1(B1), .E0(B0), .a(decodificador_2_a), .b(decodificador_2_b), .c(decodificador_2_c),
    .d(decodificador_2_d), .e(decodificador_2_e), .f(decodificador_2_f), .g(decodificador_2_g));
  _7_Segment_Display u_7_segment_display_1 (
    .g(decodificador_1_g), .f(decodificador_1_f), .a(decodificador_1_a), .b(decodificador_1_b),
    .e(decodificador_1_e), .d(decodificador_1_d), .c(decodificador_1_c));  // open: dp
  Somador4Bits somador4bits_1 (
    .Cin(1'b0), .A({A3, A2, A1, A0}), .B({B3, B2, B1, B0}), .S(somador4bits_1_s), .Cout(Cout));
  xor xor_1 (Overflow, Cout, 1'b0);
  _7_Segment_Display u_7_segment_display_2 (
    .g(decodificador_2_g), .f(decodificador_2_f), .a(decodificador_2_a), .b(decodificador_2_b),
    .e(decodificador_2_e), .d(decodificador_2_d), .c(decodificador_2_c));  // open: dp
  Decodificador decodificador_3 (
    .E3(somador4bits_1_s[3]), .E2(somador4bits_1_s[2]), .E1(somador4bits_1_s[1]), .E0(somador4bits_1_s[0]),
    .a(decodificador_3_a), .b(decodificador_3_b), .c(decodificador_3_c), .d(decodificador_3_d),
    .e(decodificador_3_e), .f(decodificador_3_f), .g(decodificador_3_g));
  _7_Segment_Display u_7_segment_display_3 (
    .g(decodificador_3_g), .f(decodificador_3_f), .a(decodificador_3_a), .b(decodificador_3_b),
    .e(decodificador_3_e), .d(decodificador_3_d), .c(decodificador_3_c));  // open: dp

  // Notes on the sheet:
  //   Calculadora 4 bits
  //   Fernando Campos Silva Dal Maria - 765053
endmodule

module Calculadora_32 (
  input  [31:0] A,
  input  [31:0] B,
  output [32:0] S
);

  Somador32Bits somador32bits_1 (.Cin(1'b0), .A(A), .B(B), .S(S[31:0]), .Cout(S[32]));
  _7_Segment_Display u_7_segment_display_1 (.b(S[32]), .c(S[32]));  // open: g, f, a, e, d, dp
  Hex_Digit_Display hex_digit_display_1 (.value(S[31:28]));  // open: dp
  Hex_Digit_Display hex_digit_display_2 (.value(S[27:24]));  // open: dp
  Hex_Digit_Display hex_digit_display_3 (.value(S[23:20]));  // open: dp
  Hex_Digit_Display hex_digit_display_4 (.value(S[19:16]));  // open: dp
  Hex_Digit_Display hex_digit_display_5 (.value(S[15:12]));  // open: dp
  Hex_Digit_Display hex_digit_display_6 (.value(S[11:8]));  // open: dp
  Hex_Digit_Display hex_digit_display_7 (.value(S[3:0]));  // open: dp
  Hex_Digit_Display hex_digit_display_8 (.value(S[7:4]));  // open: dp

  // Notes on the sheet:
  //   Calculadora 32 bits
  //   Fernando Campos Silva Dal Maria - 765053
endmodule

module MeioSomador (
  input  A,
  input  B,
  output S,
  output Cout
);

  xor xor_1 (S, A, B);
  and and_1 (Cout, A, B);

  // Notes on the sheet:
  //   Meio Somador
  //   Fernando Campos Silva Dal Maria - 765053
endmodule
