// Logisim project ULA4bits.circ as structural Verilog
module SUM (
  input  A,
  input  B,
  input  Cin,
  output S,
  output Cout
);

  wire and_1_out, and_2_out, xor_1_out;

  and and_1 (and_1_out, A, B);
  xor xor_1 (xor_1_out, A, B);
  or or_1 (Cout, and_1_out, and_2_out);
  and and_2 (and_2_out, Cin, xor_1_out);
  xor xor_2 (S, xor_1_out, Cin);

  // Notes on the sheet:
  //   Somador Completo
  //   Fernando Campos Silva Dal Maria (765053)
endmodule

module ULA1Bit (
  input  A,
  input  [1:0] OpCode,
  input  B,
  input  Binvert,
  input  Cin,
  output S,
  output Cout,
  output Overflow
);

  wire and_1_out, multiplexer_1_out, not_1_out, not_2_out, or_1_out, sum_1_s;

  Multiplexer multiplexer_1 (.in0(B), .in1(not_1_out), .out(multiplexer_1_out), .sel(Binvert));
  not not_1 (not_1_out, B);
  and and_1 (and_1_out, A, multiplexer_1_out);
  or or_1 (or_1_out, A, multiplexer_1_out);
  not not_2 (not_2_out, A);
  SUM sum_1 (.A(A), .B(multiplexer_1_out), .Cin(Cin), .S(sum_1_s), .Cout(Cout));
  Multiplexer #(.select(2)) multiplexer_2 (
    .in0(and_1_out), .in1(or_1_out), .in2(not_2_out), .in3(sum_1_s), .out(S), .sel(OpCode));
  xor xor_1 (Overflow, Cout, Cin);

  // Notes on the sheet:
  //   ULA de 1 Bit
  //   Fernando Campos Silva Dal Maria (765053)
endmodule

module ULA (
  input  Binver,
  input  [1:0] OpCode,
  input  [3:0] A,
  input  [3:0] B,
  output [3:0] S,
  output Zero,
  output Cout,
  output Overflow
);

  wire ula1bit_1_cout, ula1bit_2_cout, ula1bit_3_cout;

  ULA1Bit ula1bit_1 (
    .A(A[0]), .OpCode(OpCode), .B(B[0]), .Binvert(Binver), .Cin(Binver), .S(S[0]), .Cout(ula1bit_1_cout));  // open: Overflow
  ULA1Bit ula1bit_2 (
    .A(A[1]), .OpCode(OpCode), .B(B[1]), .Binvert(Binver), .Cin(ula1bit_1_cout), .S(S[1]),
    .Cout(ula1bit_2_cout));  // open: Overflow
  ULA1Bit ula1bit_3 (
    .A(A[2]), .OpCode(OpCode), .B(B[2]), .Binvert(Binver), .Cin(ula1bit_2_cout), .S(S[2]),
    .Cout(ula1bit_3_cout));  // open: Overflow
  ULA1Bit ula1bit_4 (
    .A(A[3]), .OpCode(OpCode), .B(B[3]), .Binvert(Binver), .Cin(ula1bit_3_cout), .S(S[3]), .Cout(Cout),
    .Overflow(Overflow));
  nor nor_1 (Zero, S[0], S[1], S[2], S[3]);

  // Notes on the sheet:
  //   ULA de 4 Bits
  //   Fernando Campos Silva Dal Maria (765053)
endmodule
